// Logisim project Computerception.circ as structural Verilog: 18 circuits, main circuit FullAdder
module main (
  input  rst
);

  wire clk, not_1_out, or_1_out, ramLoad, ramLoadGPU, ramStore;
  wire [11:0] nextLine;
  wire [15:0] CPUadress, GPUadress, ramAdress, ramData, ramOut, romOut;
  wire [31:0] displayprocessor_1_out_8, displayprocessor_1_out_9, displayprocessor_1_out_10,
       displayprocessor_1_out_11, displayprocessor_1_out_12, displayprocessor_1_out_13,
       displayprocessor_1_out_14, displayprocessor_1_out_15, displayprocessor_1_out_16,
       displayprocessor_1_out_17, displayprocessor_1_out_18, displayprocessor_1_out_19,
       displayprocessor_1_out_20, displayprocessor_1_out_21, displayprocessor_1_out_22,
       displayprocessor_1_out_23, displayprocessor_1_out_24, displayprocessor_1_out_25,
       displayprocessor_1_out_26, displayprocessor_1_out_27, displayprocessor_1_out_28,
       displayprocessor_1_out_29, displayprocessor_1_out_30, displayprocessor_1_out_31,
       displayprocessor_1_out_32, displayprocessor_1_out_33, displayprocessor_1_out_34,
       displayprocessor_1_out_35, displayprocessor_1_out_36, displayprocessor_1_out_37,
       displayprocessor_1_out_38, displayprocessor_1_out_39;

  Clock u_clk (.out(clk));
  Processador processador_1 (
    .in_1(romOut), .clk(clk), .rst(rst), .NextLine(nextLine), .out_4(CPUadress), .out_5(ramData),
    .out_6(ramStore), .out_8(ramLoad));
  RAM ram_1 (
    .in_1(ramAdress), .in_2(ramData), .out_7(ramOut), .in_4(ramStore), .in_5(clk), .in_3(or_1_out), .in_6(rst));
  or or_1 (or_1_out, ramLoadGPU, ramLoad);
  ROM #(.addrWidth(12), .dataWidth(16)) rom_1 (.addr(nextLine), .data(romOut));  // open: sel
  DotMatrix #(.matrixcols(32), .matrixrows(32), .persist(128)) dotmatrix_1 (
    .col0(displayprocessor_1_out_8), .col1(displayprocessor_1_out_9), .col2(displayprocessor_1_out_10),
    .col3(displayprocessor_1_out_11), .col4(displayprocessor_1_out_12), .col5(displayprocessor_1_out_13),
    .col6(displayprocessor_1_out_14), .col7(displayprocessor_1_out_15), .col8(displayprocessor_1_out_16),
    .col9(displayprocessor_1_out_17), .col10(displayprocessor_1_out_18), .col11(displayprocessor_1_out_19),
    .col12(displayprocessor_1_out_20), .col13(displayprocessor_1_out_21), .col14(displayprocessor_1_out_22),
    .col15(displayprocessor_1_out_23), .col16(displayprocessor_1_out_24), .col17(displayprocessor_1_out_25),
    .col18(displayprocessor_1_out_26), .col19(displayprocessor_1_out_27), .col20(displayprocessor_1_out_28),
    .col21(displayprocessor_1_out_29), .col22(displayprocessor_1_out_30), .col23(displayprocessor_1_out_31),
    .col24(displayprocessor_1_out_32), .col25(displayprocessor_1_out_33), .col26(displayprocessor_1_out_34),
    .col27(displayprocessor_1_out_35), .col28(displayprocessor_1_out_36), .col29(displayprocessor_1_out_37),
    .col30(displayprocessor_1_out_38), .col31(displayprocessor_1_out_39));
  DisplayProcessor displayprocessor_1 (
    .Store(ramStore), .Load(ramLoad), .Reset(rst), .dataIn(ramOut), .GetData(ramLoadGPU),
    .RegAdress(GPUadress), .out_8(displayprocessor_1_out_8), .out_24(displayprocessor_1_out_24),
    .out_9(displayprocessor_1_out_9), .out_25(displayprocessor_1_out_25), .out_10(displayprocessor_1_out_10),
    .out_26(displayprocessor_1_out_26), .out_11(displayprocessor_1_out_11),
    .out_27(displayprocessor_1_out_27), .out_12(displayprocessor_1_out_12),
    .out_28(displayprocessor_1_out_28), .out_13(displayprocessor_1_out_13),
    .out_29(displayprocessor_1_out_29), .out_14(displayprocessor_1_out_14),
    .out_30(displayprocessor_1_out_30), .out_15(displayprocessor_1_out_15),
    .out_31(displayprocessor_1_out_31), .out_16(displayprocessor_1_out_16),
    .out_32(displayprocessor_1_out_32), .out_17(displayprocessor_1_out_17),
    .out_33(displayprocessor_1_out_33), .out_18(displayprocessor_1_out_18),
    .out_34(displayprocessor_1_out_34), .out_19(displayprocessor_1_out_19),
    .out_35(displayprocessor_1_out_35), .out_20(displayprocessor_1_out_20),
    .out_36(displayprocessor_1_out_36), .out_21(displayprocessor_1_out_21),
    .out_37(displayprocessor_1_out_37), .out_22(displayprocessor_1_out_22),
    .out_38(displayprocessor_1_out_38), .out_23(displayprocessor_1_out_23),
    .out_39(displayprocessor_1_out_39), .clk(clk));
  not not_1 (not_1_out, ramLoadGPU);
  Transistor #(.width(16)) transistor_1 (.in(GPUadress), .out(ramAdress), .gate(not_1_out));
  Transistor #(.width(16)) transistor_2 (.in(CPUadress), .out(ramAdress), .gate(ramLoadGPU));

  // Notes on the sheet:
  //   contents of rom_1 (hex, n*v repeats v):
  //   2010 2108 1901 2240 1402 2310 1931 0 3230 213f 1431 3230 600c
  //   Endereços do Display: 1000 a 103F (hex)
endmodule

module FullAdder (
  input  a,
  input  b,
  input  ci,
  output s,
  output co
);

  wire halfsum_1_c, halfsum_1_s, halfsum_2_c;

  HalfSum halfsum_1 (.a(a), .b(b), .s(halfsum_1_s), .c(halfsum_1_c));
  HalfSum halfsum_2 (.a(halfsum_1_s), .b(ci), .s(s), .c(halfsum_2_c));
  or or_1 (co, halfsum_2_c, halfsum_1_c);
endmodule

module HalfSum (
  input  a,
  input  b,
  output s,
  output c
);

  xor xor_1 (s, a, b);
  and and_1 (c, a, b);
endmodule

module _4_bit_Ripple_Carry_Adder (
  input  ci,
  input  b0,
  input  b1,
  input  b2,
  input  b3,
  input  a0,
  input  a1,
  input  a2,
  input  a3,
  output s0,
  output s1,
  output s2,
  output s3,
  output co
);

  wire fulladder_1_co, fulladder_2_co, fulladder_3_co;

  LED led_1 (.in(s0));
  FullAdder fulladder_1 (.a(a0), .b(b0), .ci(ci), .s(s0), .co(fulladder_1_co));
  LED led_2 (.in(s1));
  FullAdder fulladder_2 (.a(a1), .b(b1), .ci(fulladder_1_co), .s(s1), .co(fulladder_2_co));
  LED led_3 (.in(s2));
  FullAdder fulladder_3 (.a(a2), .b(b2), .ci(fulladder_2_co), .s(s2), .co(fulladder_3_co));
  FullAdder fulladder_4 (.a(a3), .b(b3), .ci(fulladder_3_co), .s(s3), .co(co));
  LED led_4 (.in(s3));
  LED led_5 (.in(co));

  // Notes on the sheet:
  //   1
  //   1
  //   1
  //   2
  //   4
  //   2
  //   4
  //   2
  //   8
  //   8
  //   4
  //   8
  //   16
endmodule

module _4_bit_wirh_splitter (
  input  [3:0] in_1,
  input  [3:0] in_2,
  input  in_3,
  output [4:0] out_4
);

  wire fulladder_2_co, fulladder_3_co, fulladder_4_co;

  FullAdder fulladder_1 (.a(in_2[3]), .b(in_1[3]), .ci(fulladder_3_co), .s(out_4[3]), .co(out_4[4]));
  FullAdder fulladder_2 (.a(in_2[1]), .b(in_1[1]), .ci(fulladder_4_co), .s(out_4[1]), .co(fulladder_2_co));
  FullAdder fulladder_3 (.a(in_2[2]), .b(in_1[2]), .ci(fulladder_2_co), .s(out_4[2]), .co(fulladder_3_co));
  FullAdder fulladder_4 (.a(in_2[0]), .b(in_1[0]), .ci(in_3), .s(out_4[0]), .co(fulladder_4_co));
endmodule

module _8_bit_adder (
  input  [7:0] in_1,
  input  [7:0] in_2,
  input  ci,
  output c0,
  output [7:0] out_5
);

  wire n4_bit_ripple_carry_adder_2_co;

  _4_bit_Ripple_Carry_Adder u_4_bit_ripple_carry_adder_1 (
    .ci(n4_bit_ripple_carry_adder_2_co), .b0(in_2[4]), .a0(in_1[4]), .b1(in_2[5]), .a1(in_1[5]),
    .b2(in_1[6]), .a2(in_2[6]), .b3(in_2[7]), .a3(in_1[7]), .s0(out_5[4]), .s1(out_5[5]), .s2(out_5[6]),
    .s3(out_5[7]), .co(c0));
  // Probe on in_1
  // Probe on in_2
  _4_bit_Ripple_Carry_Adder u_4_bit_ripple_carry_adder_2 (
    .ci(ci), .b0(in_2[0]), .a0(in_1[0]), .b1(in_2[1]), .a1(in_1[1]), .b2(in_2[2]), .a2(in_1[2]),
    .b3(in_2[3]), .a3(in_1[3]), .s0(out_5[0]), .s1(out_5[1]), .s2(out_5[2]), .s3(out_5[3]),
    .co(n4_bit_ripple_carry_adder_2_co));
  // Probe on out_5
endmodule

module _16_bit_adder (
  input  [15:0] in_1,
  input  [15:0] in_2,
  input  ci,
  output co,
  output [15:0] out_5
);

  wire n8_bit_adder_2_c0;

  // Probe on in_1
  _8_bit_adder u_8_bit_adder_1 (
    .in_1(in_2[15:8]), .in_2(in_1[15:8]), .c0(co), .ci(n8_bit_adder_2_c0), .out_5(out_5[15:8]));
  // Probe on out_5
  // Probe on in_2
  _8_bit_adder u_8_bit_adder_2 (
    .in_1(in_2[7:0]), .in_2(in_1[7:0]), .c0(n8_bit_adder_2_c0), .ci(ci), .out_5(out_5[7:0]));
endmodule

module _32_bit_adder (
  input  [31:0] in_1,
  input  [31:0] in_2,
  input  ci,
  output co,
  output [31:0] out_5
);

  wire n16_bit_adder_2_co;

  // Probe on in_1
  _16_bit_adder u_16_bit_adder_1 (
    .in_1(in_2[31:16]), .in_2(in_1[31:16]), .out_5(out_5[31:16]), .ci(n16_bit_adder_2_co), .co(co));
  // Probe on out_5
  _16_bit_adder u_16_bit_adder_2 (
    .in_1(in_2[15:0]), .in_2(in_1[15:0]), .out_5(out_5[15:0]), .ci(ci), .co(n16_bit_adder_2_co));
  // Probe on in_2
endmodule

module SR_Latch (
  input  S,
  input  R,
  output Q_prime
);

  wire not_2_out, or_1_out, or_2_out;

  or or_1 (or_1_out, S, not_2_out);
  not not_1 (Q_prime, or_1_out);
  or or_2 (or_2_out, Q_prime, R);
  not not_2 (not_2_out, or_2_out);
endmodule

module D_Latch (
  input  Data,
  input  Enable,
  output Q
);

  wire and_1_out, and_2_out, not_1_out, not_2_out, not_3_out;

  not not_1 (not_1_out, Data);
  and and_1 (and_1_out, Data, Enable);
  and and_2 (and_2_out, Enable, not_1_out);
  not not_2 (not_2_out, and_1_out);
  SR_Latch sr_latch_1 (.S(not_2_out), .R(not_3_out), .Q_prime(Q));
  not not_3 (not_3_out, and_2_out);
endmodule

module Aula2 (
  input  in_1,
  input  in_2,
  input  in_3,
  input  in_4,
  input  in_5,
  input  in_6,
  input  in_7,
  input  in_8,
  input  in_9,
  input  in_10,
  input  in_11,
  input  in_12,
  output out_13,
  output out_14,
  output out_15,
  output out_16,
  output out_17,
  output out_18,
  output out_19,
  output out_20,
  output out_21,
  output Q,
  output out_23,
  output Q_prime
);

  wire and_1_out, and_2_out, and_3_out, and_4_out, and_5_out, and_6_out, and_7_out, and_8_out, and_9_out,
       and_10_out, and_11_out, and_12_out, not_1_out, not_8_out, not_9_out, not_10_out, not_11_out,
       not_12_out, not_13_out, or_1_out, or_2_out, or_3_out, or_4_out, or_5_out, or_6_out;

  and and_1 (and_1_out, in_2, out_15);
  and and_2 (and_2_out, out_13, in_4);
  or or_1 (or_1_out, in_6, out_19);
  or or_2 (or_2_out, out_17, in_8);
  not not_1 (not_1_out, in_9);
  or or_3 (or_3_out, not_1_out, out_23);
  or or_4 (or_4_out, out_21, in_9);
  Clock clock_1 ();  // open: out
  not not_2 (out_13, and_1_out);
  not not_3 (out_15, and_2_out);
  not not_4 (out_17, or_1_out);
  not not_5 (out_19, or_2_out);
  not not_6 (out_21, or_3_out);
  not not_7 (out_23, or_4_out);
  not not_8 (not_8_out, in_1);
  not not_9 (not_9_out, in_5);
  and and_3 (and_3_out, in_1, in_3);
  not not_10 (not_10_out, and_3_out);
  and and_4 (and_4_out, in_3, not_8_out);
  not not_11 (not_11_out, and_4_out);
  and and_5 (and_5_out, in_5, in_7);
  and and_6 (and_6_out, in_7, not_9_out);
  not not_12 (not_12_out, and_7_out);
  and and_7 (and_7_out, Q_prime, in_10, in_11);
  and and_8 (and_8_out, in_11, in_12, Q);
  not not_13 (not_13_out, and_8_out);
  and and_9 (and_9_out, not_10_out, out_16);
  and and_10 (and_10_out, out_14, not_11_out);
  not not_14 (out_18, or_5_out);
  or or_5 (or_5_out, and_5_out, out_20);
  or or_6 (or_6_out, out_18, and_6_out);
  not not_15 (out_20, or_6_out);
  and and_11 (and_11_out, not_12_out, Q_prime);
  and and_12 (and_12_out, Q, not_13_out);
  not not_16 (out_14, and_9_out);
  not not_17 (out_16, and_10_out);
  not not_18 (Q, and_11_out);
  not not_19 (Q_prime, and_12_out);
endmodule

module SR_Flip_Flop (
  input  D,
  input  Enable,
  input  Clock,
  output Q
);

  wire and_1_out, d_latch_1_q, not_1_out;

  and and_1 (and_1_out, Enable, Clock);
  D_Latch d_latch_1 (.Data(D), .Enable(and_1_out), .Q(d_latch_1_q));
  not not_1 (not_1_out, Clock);
  D_Latch d_latch_2 (.Data(d_latch_1_q), .Enable(not_1_out), .Q(Q));
endmodule

module Registrador (
  input  Clock,
  input  Enable,
  input  Reset,
  input  [3:0] AdressA,
  input  [3:0] AdressB,
  input  [15:0] Data,
  output [15:0] DataA,
  output [15:0] DataB
);

  wire clk, clock_1_out, en0, en1, en2, en3, en4, en5, en6, en7, en8, en9, en10, en11, en12, en13, en14, en15;
  wire [15:0] out0, out1, out2, out3, out4, out5, out6, out7, out8, out9, out10, out11, out12, out13, out14,
       out15;

  Clock clock_1 (.out(clock_1_out));
  or or_1 (clk, clock_1_out, Clock);
  Register #(.width(16)) register_1 (.D(Data), .en(en0), .Q(out0), .clk(clk), .clr(Reset));
  Register #(.width(16)) register_2 (.D(Data), .en(en4), .Q(out4), .clk(clk), .clr(Reset));
  Register #(.width(16)) register_3 (.D(Data), .en(en8), .Q(out8), .clk(clk), .clr(Reset));
  Register #(.width(16)) register_4 (.D(Data), .en(en12), .Q(out12), .clk(clk), .clr(Reset));
  Demultiplexer #(.select(4)) demultiplexer_1 (
    .out0(en0), .out1(en1), .out2(en2), .out3(en3), .out4(en4), .out5(en5), .out6(en6), .out7(en7),
    .out8(en8), .out9(en9), .out10(en10), .out11(en11), .out12(en12), .out13(en13), .out14(en14),
    .out15(en15), .in(Enable), .sel(AdressA));  // open: en
  Register #(.width(16)) register_5 (.D(Data), .en(en1), .Q(out1), .clk(clk), .clr(Reset));
  Register #(.width(16)) register_6 (.D(Data), .en(en5), .Q(out5), .clk(clk), .clr(Reset));
  Register #(.width(16)) register_7 (.D(Data), .en(en9), .Q(out9), .clk(clk), .clr(Reset));
  Register #(.width(16)) register_8 (.D(Data), .en(en13), .Q(out13), .clk(clk), .clr(Reset));
  Register #(.width(16)) register_9 (.D(Data), .en(en2), .Q(out2), .clk(clk), .clr(Reset));
  Register #(.width(16)) register_10 (.D(Data), .en(en6), .Q(out6), .clk(clk), .clr(Reset));
  Register #(.width(16)) register_11 (.D(Data), .en(en10), .Q(out10), .clk(clk), .clr(Reset));
  Register #(.width(16)) register_12 (.D(Data), .en(en14), .Q(out14), .clk(clk), .clr(Reset));
  Multiplexer #(.select(4), .width(16)) multiplexer_1 (
    .in0(out0), .in1(out1), .in2(out2), .in3(out3), .in4(out4), .in5(out5), .in6(out6), .in7(out7),
    .in8(out8), .in9(out9), .in10(out10), .in11(out11), .in12(out12), .in13(out13), .in14(out14),
    .in15(out15), .out(DataA), .sel(AdressA));  // open: en
  Register #(.width(16)) register_13 (.D(Data), .en(en3), .Q(out3), .clk(clk), .clr(Reset));
  Register #(.width(16)) register_14 (.D(Data), .en(en7), .Q(out7), .clk(clk), .clr(Reset));
  Register #(.width(16)) register_15 (.D(Data), .en(en11), .Q(out11), .clk(clk), .clr(Reset));
  Register #(.width(16)) register_16 (.D(Data), .en(en15), .Q(out15), .clk(clk), .clr(Reset));
  Multiplexer #(.select(4), .width(16)) multiplexer_2 (
    .in0(out0), .in1(out1), .in2(out2), .in3(out3), .in4(out4), .in5(out5), .in6(out6), .in7(out7),
    .in8(out8), .in9(out9), .in10(out10), .in11(out11), .in12(out12), .in13(out13), .in14(out14),
    .in15(out15), .out(DataB), .sel(AdressB));  // open: en

  // Other names for the same wires on the sheet: rst = Reset
endmodule

module ULA (
  input  [15:0] in_1,
  input  [15:0] in_2,
  input  [3:0] BitSelector,
  output [15:0] Out,
  output [1:0] C
);

  wire comparator_1_eq, comparator_1_gt, comparator_1_lt;
  wire [15:0] And, Complet, Dec, DivOut, Inc, LeftShift, MinusOut, MultOut, Not, Or, RigthShift, Squared,
       SumOut, Xor;

  Multiplier #(.width(16)) multiplier_1 (.a(in_1), .b(in_2), .out(MultOut));  // open: cin, cout
  Adder #(.width(16)) adder_1 (.a(in_1), .b(in_2), .out(SumOut));  // open: cin, cout
  Divider #(.width(16)) divider_1 (.a(in_1), .b(in_2), .out(DivOut));  // open: upper, rem
  Multiplier #(.width(16)) multiplier_2 (.a(in_1), .b(in_1), .out(Squared));  // open: cin, cout
  assign And = in_1 & in_2;  // AND_Gate and_1, 16 bits wide
  assign Or = in_1 | in_2;  // OR_Gate or_1, 16 bits wide
  assign Not = ~in_1;  // NOT_Gate not_1, 16 bits wide
  assign Xor = in_1 ^ in_2;  // XOR_Gate xor_1, 16 bits wide
  Comparator #(.width(16)) comparator_1 (
    .a(in_1), .b(in_2), .gt(comparator_1_gt), .eq(comparator_1_eq), .lt(comparator_1_lt));
  or or_2 (C[0], comparator_1_gt, comparator_1_eq);
  or or_3 (C[1], comparator_1_eq, comparator_1_lt);
  Negator #(.width(16)) negator_1 (.in(in_1), .out(Complet));
  Shifter #(.width(16)) shifter_1 (.in(in_1), .\dist (in_2[3:0]), .out(LeftShift));
  Shifter #(.width(16), .shift("lr")) shifter_2 (.in(in_1), .\dist (in_2[3:0]), .out(RigthShift));
  Adder #(.width(16)) adder_2 (.a(in_1), .b(16'h1), .out(Inc));  // open: cin, cout
  Subtractor #(.width(16)) subtractor_1 (.a(in_1), .b(16'h1), .out(Dec));  // open: bin, bout
  Multiplexer #(.select(4), .width(16)) multiplexer_1 (
    .in0(And), .in1(Or), .in2(Not), .in3(Xor), .in4(SumOut), .in5(MinusOut), .in6(MultOut), .in7(DivOut),
    .in8(Complet), .in9(LeftShift), .in10(RigthShift), .in11(Inc), .in12(Dec), .out(Out), .sel(BitSelector));  // open: in13, in14, in15, en
  // Probe on Out

  // Other names for the same wires on the sheet: a[15:0] = in_1; b[15:0] = in_2
endmodule

module Processador (
  input  [15:0] in_1,
  input  clk,
  input  rst,
  output [15:0] out_4,
  output [15:0] out_5,
  output out_6,
  output [11:0] NextLine,
  output out_8
);

  wire and_13_out, and_14_out, and_16_out, and_17_out, and_18_out, and_19_out, and_20_out, and_21_out,
       and_22_out, and_23_out, CmpAB, CmpAC, DifMov, ISCmp, ISJmp, ISmov, ISMovI, ISop, ISPush, Je, Jg, Jge,
       Jne, Movl0000, MovRAM, or_1_out, or_3_out, regen;
  wire [1:0] LastCmp, ula_1_c;
  wire [3:0] A;
  wire [11:0] adder_1_out, next;
  wire [15:0] adder_2_out, data, multiplexer_2_out, multiplexer_5_out, multiplexer_8_out, NextPointer,
       Pointer, ramOut, regAout, subtractor_1_out, ulaBin, ULAOut;

  Register #(.width(12)) PC (.D(next), .Q(NextLine), .clk(clk), .clr(rst));  // open: en
  and and_1 (ISop, in_1[12], ~in_1[13], ~in_1[14], ~in_1[15]);  // AND_Gate
  and and_2 (ISmov, ~in_1[12], in_1[13], ~in_1[14], ~in_1[15]);  // AND_Gate
  and and_3 (ISCmp, ~in_1[12], ~in_1[13], in_1[14], ~in_1[15]);  // AND_Gate
  and and_4 (ISMovI, in_1[12], in_1[13], ~in_1[14], ~in_1[15]);  // AND_Gate
  and and_5 (Movl0000, ~in_1[8], ~in_1[9], ~in_1[10], ~in_1[11]);  // AND_Gate
  and and_6 (CmpAB, ~in_1[12], ~in_1[13], in_1[14], ~in_1[15]);  // AND_Gate
  and and_7 (CmpAC, in_1[12], ~in_1[13], in_1[14], ~in_1[15]);  // AND_Gate
  and and_8 (Je, in_1[12], in_1[13], in_1[14], ~in_1[15]);  // AND_Gate
  and and_9 (Jne, ~in_1[12], ~in_1[13], ~in_1[14], in_1[15]);  // AND_Gate
  and and_10 (Jg, in_1[12], ~in_1[13], ~in_1[14], in_1[15]);  // AND_Gate
  and and_11 (Jge, ~in_1[12], in_1[13], ~in_1[14], in_1[15]);  // AND_Gate
  buf and_12 (ISPush, ~in_1[10]);  // AND_Gate AND_Gate
  Adder #(.width(12)) adder_1 (.a(NextLine), .b(12'h1), .out(adder_1_out));  // open: cin, cout
  // Probe on regAout
  Registrador registrador_1 (
    .Clock(clk), .Enable(regen), .Reset(rst), .AdressA(A), .AdressB(in_1[3:0]), .Data(data), .DataB(out_5),
    .DataA(regAout));
  // Probe on out_5
  Multiplexer #(.width(12)) multiplexer_1 (.in0(adder_1_out), .in1(in_1[11:0]), .out(next), .sel(ISJmp));  // open: en
  and and_13 (and_13_out, Je, LastCmp[0], LastCmp[1]);
  and and_14 (and_14_out, Jne, ~LastCmp[0], ~LastCmp[1]);  // AND_Gate
  not not_1 (DifMov, Movl0000);
  and and_15 (MovRAM, DifMov, ISMovI);
  Multiplexer #(.width(16)) multiplexer_2 (
    .in0(NextPointer), .in1({16{1'b1}}), .out(multiplexer_2_out), .sel(rst));  // open: en
  Register #(.width(16)) StackPointer (.D(multiplexer_2_out), .Q(Pointer), .clk(rst));  // open: en, clr
  Subtractor #(.width(16)) subtractor_1 (.a(Pointer), .b(16'h1), .out(subtractor_1_out));  // open: bin, bout
  Adder #(.width(16)) adder_2 (.a(Pointer), .b(16'h1), .out(adder_2_out));  // open: cin, cout
  and and_16 (and_16_out, ~in_1[12], in_1[13], in_1[14], ~in_1[15]);  // AND_Gate
  and and_17 (and_17_out, Jg, LastCmp[0], ~LastCmp[1]);  // AND_Gate
  and and_18 (and_18_out, LastCmp[0], ~LastCmp[1]);  // AND_Gate
  or or_1 (or_1_out, and_18_out, and_19_out);
  and and_19 (and_19_out, LastCmp[0], LastCmp[1]);
  Multiplexer #(.width(16)) multiplexer_3 (
    .in0(subtractor_1_out), .in1(adder_2_out), .out(NextPointer));  // open: sel, en
  or or_2 (ISJmp, and_16_out, and_13_out, and_14_out, and_17_out, and_20_out);
  and and_20 (and_20_out, Jge, or_1_out);
  Multiplexer #(.width(4)) multiplexer_4 (.in0(in_1[3:0]), .in1(in_1[7:4]), .sel(out_6));  // open: out, en
  ULA ula_1 (.in_1(regAout), .in_2(ulaBin), .Out(ULAOut), .BitSelector(in_1[11:8]), .C(ula_1_c));
  and and_21 (and_21_out, ISMovI, ~out_6);  // AND_Gate
  Multiplexer #(.width(16)) multiplexer_5 (
    .in0(ULAOut), .in1({{8{1'b0}}, in_1[7:0]}), .out(multiplexer_5_out), .sel(ISmov));  // open: en
  // Probe on ULAOut
  Register #(.width(2)) register_1 (.D(ula_1_c), .en(or_3_out), .Q(LastCmp), .clk(clk), .clr(rst));
  or or_3 (or_3_out, CmpAB, CmpAC);
  Multiplexer #(.width(16)) multiplexer_6 (
    .in0(out_5), .in1({{8{1'b0}}, in_1[7:0]}), .out(ulaBin), .sel(CmpAC));  // open: en
  or or_4 (regen, ISop, and_21_out, ISmov, out_8);
  Multiplexer #(.width(16)) multiplexer_7 (.in0(out_5), .in1(regAout), .out(out_4), .sel(out_6));  // open: en
  Multiplexer #(.width(16)) multiplexer_8 (
    .in0(multiplexer_5_out), .in1(ramOut), .out(multiplexer_8_out), .sel(out_8));  // open: en
  Multiplexer #(.width(16)) multiplexer_9 (
    .in0(multiplexer_8_out), .in1(out_5), .out(data), .sel(and_22_out));  // open: en
  and and_22 (and_22_out, ISMovI, Movl0000);
  Multiplexer #(.width(4)) multiplexer_10 (.in0(in_1[7:4]), .in1(in_1[11:8]), .out(A), .sel(and_23_out));  // open: en
  and and_23 (and_23_out, ~ISCmp, ~MovRAM, ~ISop);  // AND_Gate
  and and_24 (out_6, MovRAM, ~in_1[8], in_1[9], ~in_1[10], ~in_1[11]);  // AND_Gate
  and and_25 (out_8, MovRAM, in_1[8], ~in_1[9], ~in_1[10], ~in_1[11]);  // AND_Gate
  // Probe on LastCmp

  // Other names for the same wires on the sheet: crr[11:0] = NextLine; inst[15:0] = in_1; Select[3:0] = in_1[15:12];
  //   B[3:0] = in_1[3:0]; C[7:0] = in_1[7:0]; l[11:0] = in_1[11:0]; s0[3:0] = in_1[3:0]; s1[3:0] = in_1[7:4];
  //   Op[3:0] = in_1[11:8]; s2[3:0] = in_1[11:8]; ramAdress[15:0] = out_4; ramLoad = out_8; ramStore = out_6;
  //   ramData[15:0] = out_5; regBout[15:0] = out_5; ulaAin[15:0] = regAout
endmodule

module RAM (
  input  [15:0] in_1,
  input  [15:0] in_2,
  input  in_3,
  input  in_4,
  input  in_5,
  input  in_6,
  output [15:0] out_7
);

  RAM_part #(.addrWidth(16), .dataWidth(16), .bus("separate")) ram_1 (
    .addr(in_1), .din(in_2), .data(out_7), .str(in_4), .clk(in_5), .ld(in_3), .clr(in_6));  // open: sel
endmodule

module DisplayProcessor (
  input  Store,
  input  Load,
  input  clk,
  input  Reset,
  input  [15:0] dataIn,
  output GetData,
  output [15:0] RegAdress,
  output [31:0] out_8,
  output [31:0] out_9,
  output [31:0] out_10,
  output [31:0] out_11,
  output [31:0] out_12,
  output [31:0] out_13,
  output [31:0] out_14,
  output [31:0] out_15,
  output [31:0] out_16,
  output [31:0] out_17,
  output [31:0] out_18,
  output [31:0] out_19,
  output [31:0] out_20,
  output [31:0] out_21,
  output [31:0] out_22,
  output [31:0] out_23,
  output [31:0] out_24,
  output [31:0] out_25,
  output [31:0] out_26,
  output [31:0] out_27,
  output [31:0] out_28,
  output [31:0] out_29,
  output [31:0] out_30,
  output [31:0] out_31,
  output [31:0] out_32,
  output [31:0] out_33,
  output [31:0] out_34,
  output [31:0] out_35,
  output [31:0] out_36,
  output [31:0] out_37,
  output [31:0] out_38,
  output [31:0] out_39
);

  wire clk_t, crrReg, demultiplexer_1_out0, demultiplexer_1_out1, eod, not_1_out, not_2_out, not_3_out, rst,
       transistor_1_out, transistor_2_out;
  wire [15:0] counter_1_q, register_1_q, register_2_q;
  wire [31:0] adder_1_out, bit_extender_1_out, bit_extender_2_out, shift_register_1_q0, shift_register_1_q1,
       shift_register_1_q2, shift_register_1_q3, shift_register_1_q4, shift_register_1_q5,
       shift_register_1_q6, shift_register_1_q7, shift_register_1_q8, shift_register_1_q9,
       shift_register_1_q10, shift_register_1_q11, shift_register_1_q12, shift_register_1_q13,
       shift_register_1_q14, shift_register_1_q15, shift_register_1_q16, shift_register_1_q17,
       shift_register_1_q18, shift_register_1_q19, shift_register_1_q20, shift_register_1_q21,
       shift_register_1_q22, shift_register_1_q23, shift_register_1_q24, shift_register_1_q25,
       shift_register_1_q26, shift_register_1_q27, shift_register_1_q28, shift_register_1_q29,
       shift_register_1_q30, shift_register_1_q31, shifter_1_out;

  or or_1 (rst, Reset, eod);
  nor nor_1 (GetData, Store, Load);
  and and_1 (clk_t, GetData, clk);
  T_Flip_Flop t_ff_1 (.clk(clk_t), .T(1'b1), .Q(crrReg), .reset(rst));  // open: Qn, preset, en
  not not_1 (not_1_out, crrReg);
  Counter #(.width(16), .max('hffff)) counter_1 (
    .Q(counter_1_q), .clk(clk_t), .clr(rst));  // open: load, D, count, carry
  Demultiplexer demultiplexer_1 (
    .out0(demultiplexer_1_out0), .out1(demultiplexer_1_out1), .in(not_2_out), .sel(not_3_out));  // open: en
  not not_2 (not_2_out, clk_t);
  not not_3 (not_3_out, crrReg);
  Counter #(.width(16), .max('hffff)) counter_2 (.clk(not_1_out), .clr(rst));  // open: load, D, count, Q, carry
  Subtractor #(.width(16)) subtractor_1 (.a(16'h1041), .b(counter_1_q), .out(RegAdress));  // open: bin, bout
  Comparator #(.width(16)) comparator_1 (.a(counter_1_q), .b(16'h43), .eq(eod));  // open: gt, lt
  // Probe on RegAdress
  Register #(.width(16), .trigger("falling")) register_1 (
    .D(dataIn), .Q(register_1_q), .clk(transistor_1_out), .clr(rst));  // open: en
  Transistor #(.gate("br")) transistor_1 (.in(demultiplexer_1_out0), .out(transistor_1_out), .gate(rst));
  Register #(.width(16), .trigger("falling")) register_2 (
    .D(dataIn), .Q(register_2_q), .clk(transistor_2_out), .clr(rst));  // open: en
  Transistor #(.gate("br")) transistor_2 (.in(demultiplexer_1_out1), .out(transistor_2_out), .gate(rst));
  Shift_Register #(.width(32), .length(32)) shift_register_1 (
    .in(adder_1_out), .clk(crrReg), .clr(rst), .q0(shift_register_1_q0), .q1(shift_register_1_q1),
    .q2(shift_register_1_q2), .q3(shift_register_1_q3), .q4(shift_register_1_q4), .q5(shift_register_1_q5),
    .q6(shift_register_1_q6), .q7(shift_register_1_q7), .q8(shift_register_1_q8), .q9(shift_register_1_q9),
    .q10(shift_register_1_q10), .q11(shift_register_1_q11), .q12(shift_register_1_q12),
    .q13(shift_register_1_q13), .q14(shift_register_1_q14), .q15(shift_register_1_q15),
    .q16(shift_register_1_q16), .q17(shift_register_1_q17), .q18(shift_register_1_q18),
    .q19(shift_register_1_q19), .q20(shift_register_1_q20), .q21(shift_register_1_q21),
    .q22(shift_register_1_q22), .q23(shift_register_1_q23), .q24(shift_register_1_q24),
    .q25(shift_register_1_q25), .q26(shift_register_1_q26), .q27(shift_register_1_q27),
    .q28(shift_register_1_q28), .q29(shift_register_1_q29), .q30(shift_register_1_q30),
    .q31(shift_register_1_q31));  // open: shift, out, load, d0, d1, d2, d3, d4, d5, d6, d7, d8, d9, d10, d11, d12, d13, d14, d15, d16, d17, d18, d19, d20, d21, d22, d23, d24, d25, d26, d27, d28, d29, d30, d31
  Shift_Register #(.width(32), .length(32)) shift_register_2 (
    .clk(eod), .load(1'b1), .clr(Reset), .d0(shift_register_1_q0), .q0(out_8), .d1(shift_register_1_q1),
    .q1(out_9), .d2(shift_register_1_q2), .q2(out_10), .d3(shift_register_1_q3), .q3(out_11),
    .d4(shift_register_1_q4), .q4(out_12), .d5(shift_register_1_q5), .q5(out_13), .d6(shift_register_1_q6),
    .q6(out_14), .d7(shift_register_1_q7), .q7(out_15), .d8(shift_register_1_q8), .q8(out_16),
    .d9(shift_register_1_q9), .q9(out_17), .d10(shift_register_1_q10), .q10(out_18),
    .d11(shift_register_1_q11), .q11(out_19), .d12(shift_register_1_q12), .q12(out_20),
    .d13(shift_register_1_q13), .q13(out_21), .d14(shift_register_1_q14), .q14(out_22),
    .d15(shift_register_1_q15), .q15(out_23), .d16(shift_register_1_q16), .q16(out_24),
    .d17(shift_register_1_q17), .q17(out_25), .d18(shift_register_1_q18), .q18(out_26),
    .d19(shift_register_1_q19), .q19(out_27), .d20(shift_register_1_q20), .q20(out_28),
    .d21(shift_register_1_q21), .q21(out_29), .d22(shift_register_1_q22), .q22(out_30),
    .d23(shift_register_1_q23), .q23(out_31), .d24(shift_register_1_q24), .q24(out_32),
    .d25(shift_register_1_q25), .q25(out_33), .d26(shift_register_1_q26), .q26(out_34),
    .d27(shift_register_1_q27), .q27(out_35), .d28(shift_register_1_q28), .q28(out_36),
    .d29(shift_register_1_q29), .q29(out_37), .d30(shift_register_1_q30), .q30(out_38),
    .d31(shift_register_1_q31), .q31(out_39));  // open: shift, in, out
  assign bit_extender_1_out = {{16{1'b0}}, register_1_q};  // Bit_Extender bit_extender_1
  Shifter #(.width(32)) shifter_1 (.in(bit_extender_1_out), .\dist (5'b10000), .out(shifter_1_out));
  assign bit_extender_2_out = {{16{1'b0}}, register_2_q};  // Bit_Extender bit_extender_2
  Adder #(.width(32)) adder_1 (.a(shifter_1_out), .b(bit_extender_2_out), .out(adder_1_out));  // open: cin, cout
  // Probe on adder_1_out
  // Probe on shift_register_1_q0
  // Probe on shift_register_1_q29
  // Probe on shift_register_1_q31

  // Other names for the same wires on the sheet: enRAM = GetData; rstOUT = Reset
endmodule

module VRAM_Gpu (
  input  [15:0] in_1,
  input  in_2,
  input  in_3,
  output [31:0] out_4,
  output [31:0] out_5,
  output [31:0] out_6,
  output [31:0] out_7,
  output [31:0] out_8,
  output [31:0] out_9,
  output [31:0] out_10,
  output [31:0] out_11,
  output [31:0] out_12,
  output [31:0] out_13,
  output [31:0] out_14,
  output [31:0] out_15,
  output [31:0] out_16,
  output [31:0] out_17,
  output [31:0] out_18,
  output [31:0] out_19,
  output [31:0] out_20,
  output [31:0] out_21,
  output [31:0] out_22,
  output [31:0] out_23,
  output [31:0] out_24,
  output [31:0] out_25,
  output [31:0] out_26,
  output [31:0] out_27,
  output [31:0] out_28,
  output [31:0] out_29,
  output [31:0] out_30,
  output [31:0] out_31,
  output [31:0] out_32,
  output [31:0] out_33,
  output [31:0] out_34,
  output [31:0] out_35
);

  wire demultiplexer_2_out0, demultiplexer_2_out1, demultiplexer_2_out2, demultiplexer_2_out3,
       demultiplexer_2_out4, demultiplexer_2_out5, demultiplexer_2_out6, demultiplexer_2_out7,
       demultiplexer_2_out8, demultiplexer_2_out9, demultiplexer_2_out10, demultiplexer_2_out11,
       demultiplexer_2_out12, demultiplexer_2_out13, demultiplexer_2_out14, demultiplexer_2_out15,
       demultiplexer_3_out0, demultiplexer_3_out1, demultiplexer_3_out2, demultiplexer_3_out3,
       demultiplexer_3_out4, demultiplexer_3_out5, demultiplexer_3_out6, demultiplexer_3_out7,
       demultiplexer_3_out8, demultiplexer_3_out9, demultiplexer_3_out10, demultiplexer_3_out11,
       demultiplexer_3_out12, demultiplexer_3_out13, demultiplexer_3_out14, demultiplexer_3_out15,
       demultiplexer_4_out0, demultiplexer_4_out1, demultiplexer_4_out2, demultiplexer_4_out3,
       demultiplexer_4_out4, demultiplexer_4_out5, demultiplexer_4_out6, demultiplexer_4_out7,
       demultiplexer_4_out8, demultiplexer_4_out9, demultiplexer_4_out10, demultiplexer_4_out11,
       demultiplexer_4_out12, demultiplexer_4_out13, demultiplexer_4_out14, demultiplexer_4_out15,
       demultiplexer_5_out0, demultiplexer_5_out1, demultiplexer_5_out2, demultiplexer_5_out3,
       demultiplexer_5_out4, demultiplexer_5_out5, demultiplexer_5_out6, demultiplexer_5_out7,
       demultiplexer_5_out8, demultiplexer_5_out9, demultiplexer_5_out10, demultiplexer_5_out11,
       demultiplexer_5_out12, demultiplexer_5_out13, demultiplexer_5_out14, demultiplexer_5_out15, Ln1, Ln2,
       Ln3, Ln4;
  wire [1:0] LnSlct;
  wire [3:0] regSlct;
  wire [15:0] bit_extender_1_out, data, multiplier_1_out, register_1_q, register_2_q, register_3_q,
       register_4_q, register_5_q, register_6_q, register_7_q, register_8_q, register_9_q, register_10_q,
       register_11_q, register_12_q, register_13_q, register_14_q, register_15_q, register_16_q,
       register_17_q, register_18_q, register_19_q, register_20_q, register_21_q, register_22_q,
       register_23_q, register_24_q, register_25_q, register_26_q, register_27_q, register_28_q,
       register_29_q, register_30_q, register_31_q, register_32_q, register_33_q, register_34_q,
       register_35_q, register_36_q, register_37_q, register_38_q, register_39_q, register_40_q,
       register_41_q, register_42_q, register_43_q, register_44_q, register_45_q, register_46_q,
       register_47_q, register_48_q, register_49_q, register_50_q, register_51_q, register_52_q,
       register_53_q, register_54_q, register_55_q, register_56_q, register_57_q, register_58_q,
       register_59_q, register_60_q, register_61_q, register_62_q, register_63_q, register_64_q;
  wire [15:2] divider_1_out;
  wire [15:4] subtractor_1_out;
  wire [31:0] bit_extender_2_out, bit_extender_3_out, bit_extender_4_out, bit_extender_5_out,
       bit_extender_6_out, bit_extender_7_out, bit_extender_8_out, bit_extender_9_out, bit_extender_10_out,
       bit_extender_11_out, bit_extender_12_out, bit_extender_13_out, bit_extender_14_out,
       bit_extender_15_out, bit_extender_16_out, bit_extender_17_out, bit_extender_18_out,
       bit_extender_19_out, bit_extender_20_out, bit_extender_21_out, bit_extender_22_out,
       bit_extender_23_out, bit_extender_24_out, bit_extender_25_out, bit_extender_26_out,
       bit_extender_27_out, bit_extender_28_out, bit_extender_29_out, bit_extender_30_out,
       bit_extender_31_out, bit_extender_32_out, bit_extender_33_out, bit_extender_34_out,
       bit_extender_35_out, bit_extender_36_out, bit_extender_37_out, bit_extender_38_out,
       bit_extender_39_out, bit_extender_40_out, bit_extender_41_out, bit_extender_42_out,
       bit_extender_43_out, bit_extender_44_out, bit_extender_45_out, bit_extender_46_out,
       bit_extender_47_out, bit_extender_48_out, bit_extender_49_out, bit_extender_50_out,
       bit_extender_51_out, bit_extender_52_out, bit_extender_53_out, bit_extender_54_out,
       bit_extender_55_out, bit_extender_56_out, bit_extender_57_out, bit_extender_58_out,
       bit_extender_59_out, bit_extender_60_out, bit_extender_61_out, bit_extender_62_out,
       bit_extender_63_out, bit_extender_64_out, bit_extender_65_out, shifter_1_out, shifter_2_out,
       shifter_3_out, shifter_4_out, shifter_5_out, shifter_6_out, shifter_7_out, shifter_8_out,
       shifter_9_out, shifter_10_out, shifter_11_out, shifter_12_out, shifter_13_out, shifter_14_out,
       shifter_15_out, shifter_16_out, shifter_17_out, shifter_18_out, shifter_19_out, shifter_20_out,
       shifter_21_out, shifter_22_out, shifter_23_out, shifter_24_out, shifter_25_out, shifter_26_out,
       shifter_27_out, shifter_28_out, shifter_29_out, shifter_30_out, shifter_31_out, shifter_32_out;

  Demultiplexer #(.select(2)) demultiplexer_1 (
    .out0(Ln1), .out1(Ln2), .out2(Ln3), .out3(Ln4), .in(1'b1), .sel(LnSlct));  // open: en
  assign bit_extender_1_out = {{14{1'b0}}, LnSlct};  // Bit_Extender bit_extender_1
  Divider #(.width(16)) divider_1 (.a(in_1), .b(16'h10), .out({divider_1_out, LnSlct}));  // open: upper, rem
  Subtractor #(.width(16)) subtractor_1 (
    .a(in_1), .b(multiplier_1_out), .out({subtractor_1_out, regSlct}));  // open: bin, bout
  Multiplier #(.width(16)) multiplier_1 (
    .a(bit_extender_1_out), .b(16'h10), .out(multiplier_1_out));  // open: cin, cout
  Demultiplexer #(.select(4)) demultiplexer_2 (
    .out0(demultiplexer_2_out0), .out1(demultiplexer_2_out1), .out2(demultiplexer_2_out2),
    .out3(demultiplexer_2_out3), .out4(demultiplexer_2_out4), .out5(demultiplexer_2_out5),
    .out6(demultiplexer_2_out6), .out7(demultiplexer_2_out7), .out8(demultiplexer_2_out8),
    .out9(demultiplexer_2_out9), .out10(demultiplexer_2_out10), .out11(demultiplexer_2_out11),
    .out12(demultiplexer_2_out12), .out13(demultiplexer_2_out13), .out14(demultiplexer_2_out14),
    .out15(demultiplexer_2_out15), .in(1'b1), .sel(regSlct), .en(Ln1));
  Register #(.width(16)) register_1 (.D(data), .en(demultiplexer_2_out0), .Q(register_1_q), .clk(in_2), .clr(in_3));
  Register #(.width(16)) register_2 (.D(data), .en(demultiplexer_2_out1), .Q(register_2_q), .clk(in_2), .clr(in_3));
  Register #(.width(16)) register_3 (.D(data), .en(demultiplexer_2_out2), .Q(register_3_q), .clk(in_2), .clr(in_3));
  Register #(.width(16)) register_4 (.D(data), .en(demultiplexer_2_out3), .Q(register_4_q), .clk(in_2), .clr(in_3));
  Register #(.width(16)) register_5 (.D(data), .en(demultiplexer_2_out4), .Q(register_5_q), .clk(in_2), .clr(in_3));
  Register #(.width(16)) register_6 (.D(data), .en(demultiplexer_2_out5), .Q(register_6_q), .clk(in_2), .clr(in_3));
  Register #(.width(16)) register_7 (.D(data), .en(demultiplexer_2_out6), .Q(register_7_q), .clk(in_2), .clr(in_3));
  Register #(.width(16)) register_8 (.D(data), .en(demultiplexer_2_out7), .Q(register_8_q), .clk(in_2), .clr(in_3));
  Register #(.width(16)) register_9 (.D(data), .en(demultiplexer_2_out8), .Q(register_9_q), .clk(in_2), .clr(in_3));
  Register #(.width(16)) register_10 (.D(data), .en(demultiplexer_2_out9), .Q(register_10_q), .clk(in_2), .clr(in_3));
  Register #(.width(16)) register_11 (.D(data), .en(demultiplexer_2_out10), .Q(register_11_q), .clk(in_2), .clr(in_3));
  Register #(.width(16)) register_12 (.D(data), .en(demultiplexer_2_out11), .Q(register_12_q), .clk(in_2), .clr(in_3));
  Register #(.width(16)) register_13 (.D(data), .en(demultiplexer_2_out12), .Q(register_13_q), .clk(in_2), .clr(in_3));
  Register #(.width(16)) register_14 (.D(data), .en(demultiplexer_2_out13), .Q(register_14_q), .clk(in_2), .clr(in_3));
  Register #(.width(16)) register_15 (.D(data), .en(demultiplexer_2_out14), .Q(register_15_q), .clk(in_2), .clr(in_3));
  Register #(.width(16)) register_16 (.D(data), .en(demultiplexer_2_out15), .Q(register_16_q), .clk(in_2), .clr(in_3));
  assign bit_extender_2_out = {{16{1'b0}}, register_1_q};  // Bit_Extender bit_extender_2
  assign bit_extender_3_out = {{16{1'b0}}, register_2_q};  // Bit_Extender bit_extender_3
  assign bit_extender_4_out = {{16{1'b0}}, register_3_q};  // Bit_Extender bit_extender_4
  assign bit_extender_5_out = {{16{1'b0}}, register_4_q};  // Bit_Extender bit_extender_5
  assign bit_extender_6_out = {{16{1'b0}}, register_5_q};  // Bit_Extender bit_extender_6
  assign bit_extender_7_out = {{16{1'b0}}, register_6_q};  // Bit_Extender bit_extender_7
  assign bit_extender_8_out = {{16{1'b0}}, register_7_q};  // Bit_Extender bit_extender_8
  assign bit_extender_9_out = {{16{1'b0}}, register_8_q};  // Bit_Extender bit_extender_9
  assign bit_extender_10_out = {{16{1'b0}}, register_9_q};  // Bit_Extender bit_extender_10
  assign bit_extender_11_out = {{16{1'b0}}, register_10_q};  // Bit_Extender bit_extender_11
  assign bit_extender_12_out = {{16{1'b0}}, register_11_q};  // Bit_Extender bit_extender_12
  assign bit_extender_13_out = {{16{1'b0}}, register_12_q};  // Bit_Extender bit_extender_13
  assign bit_extender_14_out = {{16{1'b0}}, register_13_q};  // Bit_Extender bit_extender_14
  assign bit_extender_15_out = {{16{1'b0}}, register_14_q};  // Bit_Extender bit_extender_15
  assign bit_extender_16_out = {{16{1'b0}}, register_15_q};  // Bit_Extender bit_extender_16
  assign bit_extender_17_out = {{16{1'b0}}, register_16_q};  // Bit_Extender bit_extender_17
  Shifter #(.width(32)) shifter_1 (.in(bit_extender_2_out), .\dist (5'b10000), .out(shifter_1_out));
  Adder #(.width(32)) adder_1 (.a(shifter_1_out), .b(bit_extender_3_out), .out(out_4));  // open: cin, cout
  Shifter #(.width(32)) shifter_2 (.in(bit_extender_4_out), .\dist (5'b10000), .out(shifter_2_out));
  Adder #(.width(32)) adder_2 (.a(shifter_2_out), .b(bit_extender_5_out), .out(out_5));  // open: cin, cout
  Shifter #(.width(32)) shifter_3 (.in(bit_extender_6_out), .\dist (5'b10000), .out(shifter_3_out));
  Adder #(.width(32)) adder_3 (.a(shifter_3_out), .b(bit_extender_7_out), .out(out_6));  // open: cin, cout
  Shifter #(.width(32)) shifter_4 (.in(bit_extender_8_out), .\dist (5'b10000), .out(shifter_4_out));
  Adder #(.width(32)) adder_4 (.a(shifter_4_out), .b(bit_extender_9_out), .out(out_7));  // open: cin, cout
  Demultiplexer #(.select(4)) demultiplexer_3 (
    .out0(demultiplexer_3_out0), .out1(demultiplexer_3_out1), .out2(demultiplexer_3_out2),
    .out3(demultiplexer_3_out3), .out4(demultiplexer_3_out4), .out5(demultiplexer_3_out5),
    .out6(demultiplexer_3_out6), .out7(demultiplexer_3_out7), .out8(demultiplexer_3_out8),
    .out9(demultiplexer_3_out9), .out10(demultiplexer_3_out10), .out11(demultiplexer_3_out11),
    .out12(demultiplexer_3_out12), .out13(demultiplexer_3_out13), .out14(demultiplexer_3_out14),
    .out15(demultiplexer_3_out15), .in(1'b1), .sel(regSlct), .en(Ln2));
  Shifter #(.width(32)) shifter_5 (.in(bit_extender_10_out), .\dist (5'b10000), .out(shifter_5_out));
  Adder #(.width(32)) adder_5 (.a(shifter_5_out), .b(bit_extender_11_out), .out(out_8));  // open: cin, cout
  Shifter #(.width(32)) shifter_6 (.in(bit_extender_12_out), .\dist (5'b10000), .out(shifter_6_out));
  Adder #(.width(32)) adder_6 (.a(shifter_6_out), .b(bit_extender_13_out), .out(out_9));  // open: cin, cout
  Shifter #(.width(32)) shifter_7 (.in(bit_extender_14_out), .\dist (5'b10000), .out(shifter_7_out));
  Adder #(.width(32)) adder_7 (.a(shifter_7_out), .b(bit_extender_15_out), .out(out_10));  // open: cin, cout
  Shifter #(.width(32)) shifter_8 (.in(bit_extender_16_out), .\dist (5'b10000), .out(shifter_8_out));
  Adder #(.width(32)) adder_8 (.a(shifter_8_out), .b(bit_extender_17_out), .out(out_11));  // open: cin, cout
  Register #(.width(16)) register_17 (.D(data), .en(demultiplexer_3_out0), .Q(register_17_q), .clk(in_2), .clr(in_3));
  assign bit_extender_18_out = {{16{1'b0}}, register_17_q};  // Bit_Extender bit_extender_18
  Register #(.width(16)) register_18 (.D(data), .en(demultiplexer_3_out1), .Q(register_18_q), .clk(in_2), .clr(in_3));
  assign bit_extender_19_out = {{16{1'b0}}, register_18_q};  // Bit_Extender bit_extender_19
  assign bit_extender_20_out = {{16{1'b0}}, register_19_q};  // Bit_Extender bit_extender_20
  Register #(.width(16)) register_19 (.D(data), .en(demultiplexer_3_out2), .Q(register_19_q), .clk(in_2), .clr(in_3));
  Register #(.width(16)) register_20 (.D(data), .en(demultiplexer_3_out3), .Q(register_20_q), .clk(in_2), .clr(in_3));
  assign bit_extender_21_out = {{16{1'b0}}, register_20_q};  // Bit_Extender bit_extender_21
  Register #(.width(16)) register_21 (.D(data), .en(demultiplexer_3_out4), .Q(register_21_q), .clk(in_2), .clr(in_3));
  assign bit_extender_22_out = {{16{1'b0}}, register_21_q};  // Bit_Extender bit_extender_22
  assign bit_extender_23_out = {{16{1'b0}}, register_22_q};  // Bit_Extender bit_extender_23
  Register #(.width(16)) register_22 (.D(data), .en(demultiplexer_3_out5), .Q(register_22_q), .clk(in_2), .clr(in_3));
  assign bit_extender_24_out = {{16{1'b0}}, register_23_q};  // Bit_Extender bit_extender_24
  Register #(.width(16)) register_23 (.D(data), .en(demultiplexer_3_out6), .Q(register_23_q), .clk(in_2), .clr(in_3));
  Register #(.width(16)) register_24 (.D(data), .en(demultiplexer_3_out7), .Q(register_24_q), .clk(in_2), .clr(in_3));
  assign bit_extender_25_out = {{16{1'b0}}, register_24_q};  // Bit_Extender bit_extender_25
  Register #(.width(16)) register_25 (.D(data), .en(demultiplexer_3_out8), .Q(register_25_q), .clk(in_2), .clr(in_3));
  assign bit_extender_26_out = {{16{1'b0}}, register_25_q};  // Bit_Extender bit_extender_26
  Register #(.width(16)) register_26 (.D(data), .en(demultiplexer_3_out9), .Q(register_26_q), .clk(in_2), .clr(in_3));
  assign bit_extender_27_out = {{16{1'b0}}, register_26_q};  // Bit_Extender bit_extender_27
  assign bit_extender_28_out = {{16{1'b0}}, register_27_q};  // Bit_Extender bit_extender_28
  Register #(.width(16)) register_27 (.D(data), .en(demultiplexer_3_out10), .Q(register_27_q), .clk(in_2), .clr(in_3));
  assign bit_extender_29_out = {{16{1'b0}}, register_28_q};  // Bit_Extender bit_extender_29
  Register #(.width(16)) register_28 (.D(data), .en(demultiplexer_3_out11), .Q(register_28_q), .clk(in_2), .clr(in_3));
  assign bit_extender_30_out = {{16{1'b0}}, register_29_q};  // Bit_Extender bit_extender_30
  Register #(.width(16)) register_29 (.D(data), .en(demultiplexer_3_out12), .Q(register_29_q), .clk(in_2), .clr(in_3));
  assign bit_extender_31_out = {{16{1'b0}}, register_30_q};  // Bit_Extender bit_extender_31
  Register #(.width(16)) register_30 (.D(data), .en(demultiplexer_3_out13), .Q(register_30_q), .clk(in_2), .clr(in_3));
  assign bit_extender_32_out = {{16{1'b0}}, register_31_q};  // Bit_Extender bit_extender_32
  Register #(.width(16)) register_31 (.D(data), .en(demultiplexer_3_out14), .Q(register_31_q), .clk(in_2), .clr(in_3));
  assign bit_extender_33_out = {{16{1'b0}}, register_32_q};  // Bit_Extender bit_extender_33
  Register #(.width(16)) register_32 (.D(data), .en(demultiplexer_3_out15), .Q(register_32_q), .clk(in_2), .clr(in_3));
  Shifter #(.width(32)) shifter_9 (.in(bit_extender_18_out), .\dist (5'b10000), .out(shifter_9_out));
  Adder #(.width(32)) adder_9 (.a(shifter_9_out), .b(bit_extender_19_out), .out(out_12));  // open: cin, cout
  Shifter #(.width(32)) shifter_10 (.in(bit_extender_20_out), .\dist (5'b10000), .out(shifter_10_out));
  Adder #(.width(32)) adder_10 (.a(shifter_10_out), .b(bit_extender_21_out), .out(out_13));  // open: cin, cout
  Shifter #(.width(32)) shifter_11 (.in(bit_extender_22_out), .\dist (5'b10000), .out(shifter_11_out));
  Adder #(.width(32)) adder_11 (.a(shifter_11_out), .b(bit_extender_23_out), .out(out_14));  // open: cin, cout
  Shifter #(.width(32)) shifter_12 (.in(bit_extender_24_out), .\dist (5'b10000), .out(shifter_12_out));
  Adder #(.width(32)) adder_12 (.a(shifter_12_out), .b(bit_extender_25_out), .out(out_15));  // open: cin, cout
  Demultiplexer #(.select(4)) demultiplexer_4 (
    .out0(demultiplexer_4_out0), .out1(demultiplexer_4_out1), .out2(demultiplexer_4_out2),
    .out3(demultiplexer_4_out3), .out4(demultiplexer_4_out4), .out5(demultiplexer_4_out5),
    .out6(demultiplexer_4_out6), .out7(demultiplexer_4_out7), .out8(demultiplexer_4_out8),
    .out9(demultiplexer_4_out9), .out10(demultiplexer_4_out10), .out11(demultiplexer_4_out11),
    .out12(demultiplexer_4_out12), .out13(demultiplexer_4_out13), .out14(demultiplexer_4_out14),
    .out15(demultiplexer_4_out15), .in(1'b1), .sel(regSlct), .en(Ln3));
  Shifter #(.width(32)) shifter_13 (.in(bit_extender_26_out), .\dist (5'b10000), .out(shifter_13_out));
  Adder #(.width(32)) adder_13 (.a(shifter_13_out), .b(bit_extender_27_out), .out(out_16));  // open: cin, cout
  Shifter #(.width(32)) shifter_14 (.in(bit_extender_28_out), .\dist (5'b10000), .out(shifter_14_out));
  Adder #(.width(32)) adder_14 (.a(shifter_14_out), .b(bit_extender_29_out), .out(out_17));  // open: cin, cout
  Shifter #(.width(32)) shifter_15 (.in(bit_extender_30_out), .\dist (5'b10000), .out(shifter_15_out));
  Adder #(.width(32)) adder_15 (.a(shifter_15_out), .b(bit_extender_31_out), .out(out_18));  // open: cin, cout
  Shifter #(.width(32)) shifter_16 (.in(bit_extender_32_out), .\dist (5'b10000), .out(shifter_16_out));
  Adder #(.width(32)) adder_16 (.a(shifter_16_out), .b(bit_extender_33_out), .out(out_19));  // open: cin, cout
  assign bit_extender_34_out = {{16{1'b0}}, register_33_q};  // Bit_Extender bit_extender_34
  Register #(.width(16)) register_33 (.D(data), .en(demultiplexer_4_out0), .Q(register_33_q), .clk(in_2), .clr(in_3));
  assign bit_extender_35_out = {{16{1'b0}}, register_34_q};  // Bit_Extender bit_extender_35
  Register #(.width(16)) register_34 (.D(data), .en(demultiplexer_4_out1), .Q(register_34_q), .clk(in_2), .clr(in_3));
  Register #(.width(16)) register_35 (.D(data), .en(demultiplexer_4_out2), .Q(register_35_q), .clk(in_2), .clr(in_3));
  assign bit_extender_36_out = {{16{1'b0}}, register_35_q};  // Bit_Extender bit_extender_36
  Register #(.width(16)) register_36 (.D(data), .en(demultiplexer_4_out3), .Q(register_36_q), .clk(in_2), .clr(in_3));
  assign bit_extender_37_out = {{16{1'b0}}, register_36_q};  // Bit_Extender bit_extender_37
  assign bit_extender_38_out = {{16{1'b0}}, register_37_q};  // Bit_Extender bit_extender_38
  Register #(.width(16)) register_37 (.D(data), .en(demultiplexer_4_out4), .Q(register_37_q), .clk(in_2), .clr(in_3));
  Register #(.width(16)) register_38 (.D(data), .en(demultiplexer_4_out5), .Q(register_38_q), .clk(in_2), .clr(in_3));
  assign bit_extender_39_out = {{16{1'b0}}, register_38_q};  // Bit_Extender bit_extender_39
  assign bit_extender_40_out = {{16{1'b0}}, register_39_q};  // Bit_Extender bit_extender_40
  Register #(.width(16)) register_39 (.D(data), .en(demultiplexer_4_out6), .Q(register_39_q), .clk(in_2), .clr(in_3));
  Register #(.width(16)) register_40 (.D(data), .en(demultiplexer_4_out7), .Q(register_40_q), .clk(in_2), .clr(in_3));
  assign bit_extender_41_out = {{16{1'b0}}, register_40_q};  // Bit_Extender bit_extender_41
  Register #(.width(16)) register_41 (.D(data), .en(demultiplexer_4_out8), .Q(register_41_q), .clk(in_2), .clr(in_3));
  assign bit_extender_42_out = {{16{1'b0}}, register_41_q};  // Bit_Extender bit_extender_42
  assign bit_extender_43_out = {{16{1'b0}}, register_42_q};  // Bit_Extender bit_extender_43
  Register #(.width(16)) register_42 (.D(data), .en(demultiplexer_4_out9), .Q(register_42_q), .clk(in_2), .clr(in_3));
  assign bit_extender_44_out = {{16{1'b0}}, register_43_q};  // Bit_Extender bit_extender_44
  Register #(.width(16)) register_43 (.D(data), .en(demultiplexer_4_out10), .Q(register_43_q), .clk(in_2), .clr(in_3));
  Register #(.width(16)) register_44 (.D(data), .en(demultiplexer_4_out11), .Q(register_44_q), .clk(in_2), .clr(in_3));
  assign bit_extender_45_out = {{16{1'b0}}, register_44_q};  // Bit_Extender bit_extender_45
  Register #(.width(16)) register_45 (.D(data), .en(demultiplexer_4_out12), .Q(register_45_q), .clk(in_2), .clr(in_3));
  assign bit_extender_46_out = {{16{1'b0}}, register_45_q};  // Bit_Extender bit_extender_46
  Register #(.width(16)) register_46 (.D(data), .en(demultiplexer_4_out13), .Q(register_46_q), .clk(in_2), .clr(in_3));
  assign bit_extender_47_out = {{16{1'b0}}, register_46_q};  // Bit_Extender bit_extender_47
  assign bit_extender_48_out = {{16{1'b0}}, register_47_q};  // Bit_Extender bit_extender_48
  Register #(.width(16)) register_47 (.D(data), .en(demultiplexer_4_out14), .Q(register_47_q), .clk(in_2), .clr(in_3));
  assign bit_extender_49_out = {{16{1'b0}}, register_48_q};  // Bit_Extender bit_extender_49
  Register #(.width(16)) register_48 (.D(data), .en(demultiplexer_4_out15), .Q(register_48_q), .clk(in_2), .clr(in_3));
  Shifter #(.width(32)) shifter_17 (.in(bit_extender_34_out), .\dist (5'b10000), .out(shifter_17_out));
  Adder #(.width(32)) adder_17 (.a(shifter_17_out), .b(bit_extender_35_out), .out(out_20));  // open: cin, cout
  Shifter #(.width(32)) shifter_18 (.in(bit_extender_36_out), .\dist (5'b10000), .out(shifter_18_out));
  Adder #(.width(32)) adder_18 (.a(shifter_18_out), .b(bit_extender_37_out), .out(out_21));  // open: cin, cout
  Shifter #(.width(32)) shifter_19 (.in(bit_extender_38_out), .\dist (5'b10000), .out(shifter_19_out));
  Adder #(.width(32)) adder_19 (.a(shifter_19_out), .b(bit_extender_39_out), .out(out_22));  // open: cin, cout
  Shifter #(.width(32)) shifter_20 (.in(bit_extender_40_out), .\dist (5'b10000), .out(shifter_20_out));
  Adder #(.width(32)) adder_20 (.a(shifter_20_out), .b(bit_extender_41_out), .out(out_23));  // open: cin, cout
  Shifter #(.width(32)) shifter_21 (.in(bit_extender_42_out), .\dist (5'b10000), .out(shifter_21_out));
  Adder #(.width(32)) adder_21 (.a(shifter_21_out), .b(bit_extender_43_out), .out(out_24));  // open: cin, cout
  Shifter #(.width(32)) shifter_22 (.in(bit_extender_44_out), .\dist (5'b10000), .out(shifter_22_out));
  Adder #(.width(32)) adder_22 (.a(shifter_22_out), .b(bit_extender_45_out), .out(out_25));  // open: cin, cout
  Shifter #(.width(32)) shifter_23 (.in(bit_extender_46_out), .\dist (5'b10000), .out(shifter_23_out));
  Adder #(.width(32)) adder_23 (.a(shifter_23_out), .b(bit_extender_47_out), .out(out_26));  // open: cin, cout
  Shifter #(.width(32)) shifter_24 (.in(bit_extender_48_out), .\dist (5'b10000), .out(shifter_24_out));
  Adder #(.width(32)) adder_24 (.a(shifter_24_out), .b(bit_extender_49_out), .out(out_27));  // open: cin, cout
  Demultiplexer #(.select(4)) demultiplexer_5 (
    .out0(demultiplexer_5_out0), .out1(demultiplexer_5_out1), .out2(demultiplexer_5_out2),
    .out3(demultiplexer_5_out3), .out4(demultiplexer_5_out4), .out5(demultiplexer_5_out5),
    .out6(demultiplexer_5_out6), .out7(demultiplexer_5_out7), .out8(demultiplexer_5_out8),
    .out9(demultiplexer_5_out9), .out10(demultiplexer_5_out10), .out11(demultiplexer_5_out11),
    .out12(demultiplexer_5_out12), .out13(demultiplexer_5_out13), .out14(demultiplexer_5_out14),
    .out15(demultiplexer_5_out15), .in(1'b1), .sel(regSlct), .en(Ln4));
  Register #(.width(16)) register_49 (.D(data), .en(demultiplexer_5_out0), .Q(register_49_q), .clk(in_2), .clr(in_3));
  assign bit_extender_50_out = {{16{1'b0}}, register_49_q};  // Bit_Extender bit_extender_50
  assign bit_extender_51_out = {{16{1'b0}}, register_50_q};  // Bit_Extender bit_extender_51
  Register #(.width(16)) register_50 (.D(data), .en(demultiplexer_5_out1), .Q(register_50_q), .clk(in_2), .clr(in_3));
  assign bit_extender_52_out = {{16{1'b0}}, register_51_q};  // Bit_Extender bit_extender_52
  Register #(.width(16)) register_51 (.D(data), .en(demultiplexer_5_out2), .Q(register_51_q), .clk(in_2), .clr(in_3));
  assign bit_extender_53_out = {{16{1'b0}}, register_52_q};  // Bit_Extender bit_extender_53
  Register #(.width(16)) register_52 (.D(data), .en(demultiplexer_5_out3), .Q(register_52_q), .clk(in_2), .clr(in_3));
  Register #(.width(16)) register_53 (.D(data), .en(demultiplexer_5_out4), .Q(register_53_q), .clk(in_2), .clr(in_3));
  assign bit_extender_54_out = {{16{1'b0}}, register_53_q};  // Bit_Extender bit_extender_54
  assign bit_extender_55_out = {{16{1'b0}}, register_54_q};  // Bit_Extender bit_extender_55
  Register #(.width(16)) register_54 (.D(data), .en(demultiplexer_5_out5), .Q(register_54_q), .clk(in_2), .clr(in_3));
  assign bit_extender_56_out = {{16{1'b0}}, register_55_q};  // Bit_Extender bit_extender_56
  Register #(.width(16)) register_55 (.D(data), .en(demultiplexer_5_out6), .Q(register_55_q), .clk(in_2), .clr(in_3));
  Register #(.width(16)) register_56 (.D(data), .en(demultiplexer_5_out7), .Q(register_56_q), .clk(in_2), .clr(in_3));
  assign bit_extender_57_out = {{16{1'b0}}, register_56_q};  // Bit_Extender bit_extender_57
  Register #(.width(16)) register_57 (.D(data), .en(demultiplexer_5_out8), .Q(register_57_q), .clk(in_2), .clr(in_3));
  assign bit_extender_58_out = {{16{1'b0}}, register_57_q};  // Bit_Extender bit_extender_58
  assign bit_extender_59_out = {{16{1'b0}}, register_58_q};  // Bit_Extender bit_extender_59
  Register #(.width(16)) register_58 (.D(data), .en(demultiplexer_5_out9), .Q(register_58_q), .clk(in_2), .clr(in_3));
  Register #(.width(16)) register_59 (.D(data), .en(demultiplexer_5_out10), .Q(register_59_q), .clk(in_2), .clr(in_3));
  assign bit_extender_60_out = {{16{1'b0}}, register_59_q};  // Bit_Extender bit_extender_60
  assign bit_extender_61_out = {{16{1'b0}}, register_60_q};  // Bit_Extender bit_extender_61
  Register #(.width(16)) register_60 (.D(data), .en(demultiplexer_5_out11), .Q(register_60_q), .clk(in_2), .clr(in_3));
  assign bit_extender_62_out = {{16{1'b0}}, register_61_q};  // Bit_Extender bit_extender_62
  Register #(.width(16)) register_61 (.D(data), .en(demultiplexer_5_out12), .Q(register_61_q), .clk(in_2), .clr(in_3));
  Register #(.width(16)) register_62 (.D(data), .en(demultiplexer_5_out13), .Q(register_62_q), .clk(in_2), .clr(in_3));
  assign bit_extender_63_out = {{16{1'b0}}, register_62_q};  // Bit_Extender bit_extender_63
  assign bit_extender_64_out = {{16{1'b0}}, register_63_q};  // Bit_Extender bit_extender_64
  Register #(.width(16)) register_63 (.D(data), .en(demultiplexer_5_out14), .Q(register_63_q), .clk(in_2), .clr(in_3));
  assign bit_extender_65_out = {{16{1'b0}}, register_64_q};  // Bit_Extender bit_extender_65
  Register #(.width(16)) register_64 (.D(data), .en(demultiplexer_5_out15), .Q(register_64_q), .clk(in_2), .clr(in_3));
  Shifter #(.width(32)) shifter_25 (.in(bit_extender_50_out), .\dist (5'b10000), .out(shifter_25_out));
  Adder #(.width(32)) adder_25 (.a(shifter_25_out), .b(bit_extender_51_out), .out(out_28));  // open: cin, cout
  Shifter #(.width(32)) shifter_26 (.in(bit_extender_52_out), .\dist (5'b10000), .out(shifter_26_out));
  Adder #(.width(32)) adder_26 (.a(shifter_26_out), .b(bit_extender_53_out), .out(out_29));  // open: cin, cout
  Shifter #(.width(32)) shifter_27 (.in(bit_extender_54_out), .\dist (5'b10000), .out(shifter_27_out));
  Adder #(.width(32)) adder_27 (.a(shifter_27_out), .b(bit_extender_55_out), .out(out_30));  // open: cin, cout
  Shifter #(.width(32)) shifter_28 (.in(bit_extender_56_out), .\dist (5'b10000), .out(shifter_28_out));
  Adder #(.width(32)) adder_28 (.a(shifter_28_out), .b(bit_extender_57_out), .out(out_31));  // open: cin, cout
  Shifter #(.width(32)) shifter_29 (.in(bit_extender_58_out), .\dist (5'b10000), .out(shifter_29_out));
  Adder #(.width(32)) adder_29 (.a(shifter_29_out), .b(bit_extender_59_out), .out(out_32));  // open: cin, cout
  Shifter #(.width(32)) shifter_30 (.in(bit_extender_60_out), .\dist (5'b10000), .out(shifter_30_out));
  Adder #(.width(32)) adder_30 (.a(shifter_30_out), .b(bit_extender_61_out), .out(out_33));  // open: cin, cout
  Shifter #(.width(32)) shifter_31 (.in(bit_extender_62_out), .\dist (5'b10000), .out(shifter_31_out));
  Adder #(.width(32)) adder_31 (.a(shifter_31_out), .b(bit_extender_63_out), .out(out_34));  // open: cin, cout
  Shifter #(.width(32)) shifter_32 (.in(bit_extender_64_out), .\dist (5'b10000), .out(shifter_32_out));
  Adder #(.width(32)) adder_32 (.a(shifter_32_out), .b(bit_extender_65_out), .out(out_35));  // open: cin, cout

  // Other names for the same wires on the sheet: Adress[15:0] = in_1; clk = in_2; reg0[31:0] = out_4;
  //   reg1[31:0] = out_5; reg2[31:0] = out_6; reg3[31:0] = out_7; reg4[31:0] = out_8; reg5[31:0] = out_9;
  //   reg6[31:0] = out_10; reg7[31:0] = out_11; reg8[31:0] = out_12; reg9[31:0] = out_13; reg10[31:0] = out_14;
  //   reg11[31:0] = out_15; reg12[31:0] = out_16; reg13[31:0] = out_17; reg14[31:0] = out_18; reg15[31:0] = out_19;
  //   reg16[31:0] = out_20; reg17[31:0] = out_21; reg18[31:0] = out_22; reg19[31:0] = out_23; reg20[31:0] = out_24;
  //   reg21[31:0] = out_25; reg22[31:0] = out_26; reg23[31:0] = out_27; reg24[31:0] = out_28; reg25[31:0] = out_29;
  //   reg26[31:0] = out_30; reg27[31:0] = out_31; reg28[31:0] = out_32; reg29[31:0] = out_33; reg30[31:0] = out_34;
  //   reg31[31:0] = out_35; rst = in_3
endmodule
