// Logisim project NewPC.circ as structural Verilog
module Register_Bank (
  input  [3:0] A,
  input  [3:0] B,
  input  clk,
  input  rst,
  input  en,
  input  [15:0] data,
  output [15:0] DataA,
  output [15:0] DataB
);

  wire demultiplexer_1_out0, demultiplexer_1_out1, demultiplexer_1_out2, demultiplexer_1_out3,
       demultiplexer_1_out4, demultiplexer_1_out5, demultiplexer_1_out6, demultiplexer_1_out7,
       demultiplexer_2_out0, demultiplexer_2_out1, demultiplexer_2_out2, demultiplexer_2_out3,
       demultiplexer_2_out4, demultiplexer_2_out5, demultiplexer_2_out6, demultiplexer_2_out7, not_1_out;
  wire [15:0] out0, out1, out2, out3, out4, out5, out6, out7, out8, out9, out10, out11, out12, out13, out14,
       out15;

  Demultiplexer #(.select(3), .disabled(0)) demultiplexer_1 (
    .out0(demultiplexer_1_out0), .out1(demultiplexer_1_out1), .out2(demultiplexer_1_out2),
    .out3(demultiplexer_1_out3), .out4(demultiplexer_1_out4), .out5(demultiplexer_1_out5),
    .out6(demultiplexer_1_out6), .out7(demultiplexer_1_out7), .in(en), .sel(A[2:0]), .en(not_1_out));
  not not_1 (not_1_out, A[3]);
  Register #(.width(16)) register_1 (.D(data), .en(demultiplexer_1_out0), .Q(out0), .clk(clk), .clr(rst));
  Register #(.width(16)) register_2 (.D(data), .en(demultiplexer_1_out1), .Q(out1), .clk(clk), .clr(rst));
  Register #(.width(16)) register_3 (.D(data), .en(demultiplexer_1_out2), .Q(out2), .clk(clk), .clr(rst));
  Register #(.width(16)) register_4 (.D(data), .en(demultiplexer_1_out3), .Q(out3), .clk(clk), .clr(rst));
  Register #(.width(16)) register_5 (.D(data), .en(demultiplexer_1_out4), .Q(out4), .clk(clk), .clr(rst));
  Register #(.width(16)) register_6 (.D(data), .en(demultiplexer_1_out5), .Q(out5), .clk(clk), .clr(rst));
  Register #(.width(16)) register_7 (.D(data), .en(demultiplexer_1_out6), .Q(out6), .clk(clk), .clr(rst));
  Register #(.width(16)) register_8 (.D(data), .en(demultiplexer_1_out7), .Q(out7), .clk(clk), .clr(rst));
  Demultiplexer #(.select(3), .disabled(0)) demultiplexer_2 (
    .out0(demultiplexer_2_out0), .out1(demultiplexer_2_out1), .out2(demultiplexer_2_out2),
    .out3(demultiplexer_2_out3), .out4(demultiplexer_2_out4), .out5(demultiplexer_2_out5),
    .out6(demultiplexer_2_out6), .out7(demultiplexer_2_out7), .in(en), .sel(A[2:0]), .en(A[3]));
  Register #(.width(16)) register_9 (.D(data), .en(demultiplexer_2_out0), .Q(out8), .clk(clk), .clr(rst));
  Register #(.width(16)) register_10 (.D(data), .en(demultiplexer_2_out1), .Q(out9), .clk(clk), .clr(rst));
  Register #(.width(16)) register_11 (.D(data), .en(demultiplexer_2_out2), .Q(out10), .clk(clk), .clr(rst));
  Register #(.width(16)) register_12 (.D(data), .en(demultiplexer_2_out3), .Q(out11), .clk(clk), .clr(rst));
  Register #(.width(16)) register_13 (.D(data), .en(demultiplexer_2_out4), .Q(out12), .clk(clk), .clr(rst));
  Register #(.width(16)) register_14 (.D(data), .en(demultiplexer_2_out5), .Q(out13), .clk(clk), .clr(rst));
  Register #(.width(16)) register_15 (.D(data), .en(demultiplexer_2_out6), .Q(out14), .clk(clk), .clr(rst));
  Register #(.width(16)) register_16 (.D(data), .en(demultiplexer_2_out7), .Q(out15), .clk(clk), .clr(rst));
  Multiplexer #(.select(4), .width(16)) multiplexer_1 (
    .in0(out0), .in1(out1), .in2(out2), .in3(out3), .in4(out4), .in5(out5), .in6(out6), .in7(out7),
    .in8(out8), .in9(out9), .in10(out10), .in11(out11), .in12(out12), .in13(out13), .in14(out14),
    .in15(out15), .out(DataA), .sel(A));  // open: en
  Multiplexer #(.select(4), .width(16)) multiplexer_2 (
    .in0(out0), .in1(out1), .in2(out2), .in3(out3), .in4(out4), .in5(out5), .in6(out6), .in7(out7),
    .in8(out8), .in9(out9), .in10(out10), .in11(out11), .in12(out12), .in13(out13), .in14(out14),
    .in15(out15), .out(DataB), .sel(B));  // open: en

  // Other names for the same wires on the sheet: Ln = A[3]; reg[2:0] = A[2:0]
endmodule

module ULA (
  input  [15:0] in_1,
  input  [15:0] in_2,
  input  [3:0] BitSelector,
  output [15:0] Out,
  output C0,
  output [1:0] C
);

  wire comparator_1_eq, comparator_1_gt, comparator_1_lt;
  wire [15:0] And, Complet, Dec, DivOut, Inc, LeftShift, MinusOut, MultOut, Not, Or, RigthShift, Squared,
       SumOut, Xor;

  Multiplier #(.width(16)) multiplier_1 (.a(in_1), .b(in_2), .out(MultOut));  // open: cin, cout
  Adder #(.width(16)) adder_1 (.a(in_1), .b(in_2), .out(SumOut));  // open: cin, cout
  Divider #(.width(16)) divider_1 (.a(in_1), .b(in_2), .out(DivOut));  // open: upper, rem
  Multiplier #(.width(16)) multiplier_2 (.a(in_1), .b(in_1), .out(Squared));  // open: cin, cout
  assign And = in_1 & in_2;  // AND_Gate and_1, 16 bits wide
  assign Or = in_1 | in_2;  // OR_Gate or_1, 16 bits wide
  assign Not = ~in_1;  // NOT_Gate not_1, 16 bits wide
  assign Xor = in_1 ^ in_2;  // XOR_Gate xor_1, 16 bits wide
  Comparator #(.width(16)) comparator_1 (
    .a(in_1), .b(in_2), .gt(comparator_1_gt), .eq(comparator_1_eq), .lt(comparator_1_lt));
  or or_2 (C[0], comparator_1_gt, comparator_1_eq);
  or or_3 (C[1], comparator_1_eq, comparator_1_lt);
  Negator #(.width(16)) negator_1 (.in(in_1), .out(Complet));
  Shifter #(.width(16)) shifter_1 (.in(in_1), .\dist (in_2[3:0]), .out(LeftShift));
  Shifter #(.width(16), .shift("lr")) shifter_2 (.in(in_1), .\dist (in_2[3:0]), .out(RigthShift));
  Adder #(.width(16)) adder_2 (.a(in_1), .b(16'h1), .out(Inc));  // open: cin, cout
  Subtractor #(.width(16)) subtractor_1 (.a(in_1), .b(16'h1), .out(Dec));  // open: bin, bout
  Comparator #(.width(16)) comparator_2 (.a(Out), .b({16{1'b0}}), .eq(C0));  // open: gt, lt
  Multiplexer #(.select(4), .width(16)) multiplexer_1 (
    .in0(And), .in1(Or), .in2(Not), .in3(Xor), .in4(SumOut), .in5(MinusOut), .in6(MultOut), .in7(DivOut),
    .in8(Complet), .in9(LeftShift), .in10(RigthShift), .in11(Inc), .in12(Dec), .out(Out), .sel(BitSelector));  // open: in13, in14, in15, en

  // Other names for the same wires on the sheet: a[15:0] = in_1; b[15:0] = in_2
endmodule

module CPU (
  input  [15:0] in,
  input  clk,
  input  rst
);

  wire and_1_out, and_2_out, and_3_out, call, cmp, cmp_prime, en, je, jg, jge, jmp, jne, jz, mov, mov_prime,
       op, or_2_out, or_3_out, ret, uC0, ula_1_c0;
  wire [1:0] uC, ula_1_c;
  wire [3:0] rAi;
  wire [15:0] Din, rAo, rBo, uBi, uO;

  Demultiplexer #(.select(4)) demultiplexer_1 (
    .out1(op), .out2(mov), .out3(mov_prime), .out4(cmp), .out5(cmp_prime), .out6(jmp), .out7(je), .out8(jne),
    .out9(jg), .out10(jge), .out11(jz), .out12(call), .out13(ret), .in(1'b1), .sel(in[15:12]));  // open: out0, out14, out15, en
  or or_1 (en, op, and_1_out);
  and and_1 (and_1_out, mov_prime, ~in[9], ~in[11]);  // AND_Gate
  Multiplexer #(.width(4)) multiplexer_1 (.in0(in[11:8]), .in1(in[7:4]), .out(rAi), .sel(or_2_out));  // open: en
  and and_2 (and_2_out, in[12], ~in[14], ~in[15]);  // AND_Gate
  or or_2 (or_2_out, and_2_out, and_3_out);
  and and_3 (and_3_out, ~in[12], ~in[13], in[14], ~in[15]);  // AND_Gate
  // Probe on rAo
  // Probe on rBo
  Register_Bank register_bank_1 (
    .A(rAi), .B(in[3:0]), .clk(clk), .rst(rst), .en(en), .data(Din), .DataA(rAo), .DataB(rBo));
  Multiplexer #(.width(16)) multiplexer_2 (
    .in0(rBo), .in1({{8{1'b0}}, in[7:0]}), .out(uBi), .sel(cmp_prime));  // open: en
  ULA ula_1 (.in_1(rAo), .in_2(uBi), .Out(uO), .C(ula_1_c), .BitSelector(in[11:8]), .C0(ula_1_c0));
  or or_3 (or_3_out, cmp, cmp_prime);
  Register #(.width(2)) register_1 (.D(ula_1_c), .en(or_3_out), .Q(uC), .clk(clk), .clr(rst));
  Register #(.width(1)) register_2 (.D(ula_1_c0), .en(or_3_out), .Q(uC0), .clk(clk), .clr(rst));

  // Other names for the same wires on the sheet: s0[3:0] = in[15:12]; c[7:0] = in[7:0]; l[11:0] = in[11:0];
  //   rBi[3:0] = in[3:0]; s3[3:0] = in[3:0]; s2[3:0] = in[7:4]; s1[3:0] = in[11:8]; uAi[15:0] = rAo
endmodule

module RAM (
  input  [15:0] in_1,
  input  [15:0] in_2,
  input  in_3,
  input  in_4,
  input  in_5,
  input  in_6,
  output [15:0] out_7
);

  RAM_part #(.addrWidth(16), .dataWidth(16), .bus("separate")) ram_1 (
    .addr(in_1), .din(in_2), .data(out_7), .str(in_3), .clk(in_4), .ld(in_5), .clr(in_6));  // open: sel
endmodule
